# Fritzing sketch Fritzing_sketch (saved by Fritzing 0.9.9b)
breadboards: 1

parts:
  M1 = DOIT Esp32 DevKit v1 (30 pins long, 11 pins width) [part_number=ESP32S-PIN30]
  YwRobot_Power_Supply1 = YwRobot Breadboard Power Supply [part_number=545043]
  Grove1 = Grove OLED 128x96
  RHT1 = Humidity and Temperature Sensor RHT03
  R1 = Rotary Potentiometer (Small) [maximum_resistance=100kΩ package=THT]
  HC-SR04_Sensor_1 = HC-SR04 Ultrasonic Distance Sensor

nets:
  N1: M1.D4, RHT1.Data-signal
  N2: M1.D21, Grove1.SDA
  N3: M1.D22, Grove1.SCL
  N4: M1.D34, R1.wiper
  N5: M1.D14, HC-SR04_Sensor_1.TRIG
  N6: M1.D13, HC-SR04_Sensor_1.ECHO
  N7: YwRobot_Power_Supply1.VCC#5, YwRobot_Power_Supply1.VCC#6
  VCC: YwRobot_Power_Supply1.VCC#9, YwRobot_Power_Supply1.VCC#10, Grove1.VCC, RHT1.Vcc, R1.leg2, HC-SR04_Sensor_1.VCC
  N8: YwRobot_Power_Supply1.GND#11, YwRobot_Power_Supply1.GND#12
  GND: YwRobot_Power_Supply1.GND#13, YwRobot_Power_Supply1.GND#14, Grove1.GND, RHT1.GND_2, R1.leg1, HC-SR04_Sensor_1.GND

custom parts:
  DOIT Esp32 DevKit v1 (30 pins long, 11 pins width): The DOIT Esp32 DevKit v1 is one of the development board created by DOIT to evaluate the ESP-WROOM-32 module. It is based on the ESP32 microcontroller that boasts Wifi, Bluetooth, Ethernet and Low Power support all in a single chip. (vanepp) made breadboard work, adjusted pin numbering and labels and reduced size of schematic and cleaned up pcb. This chip is 30pins long (2 x15) and 11 pins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
  YwRobot Breadboard Power Supply: The YwRobot Breadboard Power Supply (MB-V2) has two power rails; they can be 5V or 3V3. Power to the module can be provided through the female USB socket or through the A10 (female) 2.1mm power jack.
